# Fritzing sketch circuit (saved by Fritzing 0.9.6b)
breadboards: 1

parts:
  MH-ET_LIVE_ESP32_DEVKIT1 = MH-ET LIVE ESP32 DEVKIT 38 pins
  Componente2 = Triple Axis Accelerometer Breakout - ADXL345

nets:
  3V3: MH-ET_LIVE_ESP32_DEVKIT1.3V3, Componente2.VCC
  N1: MH-ET_LIVE_ESP32_DEVKIT1.IO14, Componente2.SCL
  N2: MH-ET_LIVE_ESP32_DEVKIT1.IO12, Componente2.SDO
  N3: MH-ET_LIVE_ESP32_DEVKIT1.GND#58, Componente2.GND
  N4: MH-ET_LIVE_ESP32_DEVKIT1.IO13, Componente2.SDA
  N5: MH-ET_LIVE_ESP32_DEVKIT1.IO15, Componente2.CS

custom parts:
  MH-ET LIVE ESP32 DEVKIT 38 pins: http://mh.nodebb.com/topic/2/mh-et-live-esp32-devkit
